// Logisim project CPE142_HW05_TheImmediateOperand.circ as structural Verilog: 1 circuit, main circuit main
module main (
  input  Read__1____Write__0__Pin
);

  wire Clear_Counter_out, Clear_Memory_out, Clear_TTY_out, clock_1_out, not_1_out;
  wire [3:0] multiplexer_2_out;
  wire [6:0] bit_extender_2_out;
  wire [15:0] adder_1_out, adder_2_out, bit_extender_1_out, multiplexer_1_out, ram_1_data, Register_q;

  Register #(.width(16)) Register (
    .D(multiplexer_1_out), .en(1'b1), .Q(Register_q), .clk(clock_1_out), .clr(Clear_Counter_out));
  Clock clock_1 (.out(clock_1_out));
  Button Clear_Counter (.out(Clear_Counter_out));
  Adder #(.width(16)) adder_1 (.a(Register_q), .b(16'h1), .out(adder_1_out));  // open: cin, cout
  Adder #(.width(16)) adder_2 (.a(Register_q), .b(bit_extender_1_out), .out(adder_2_out));  // open: cin, cout
  not not_1 (not_1_out, Read__1____Write__0__Pin);
  Multiplexer #(.width(16)) multiplexer_1 (
    .in0(adder_1_out), .in1(adder_2_out), .out(multiplexer_1_out), .sel(ram_1_data[1]));  // open: en
  RAM #(.addrWidth(16), .dataWidth(16), .bus("separate")) ram_1 (
    .addr(Register_q), .data(ram_1_data), .str(not_1_out), .clk(clock_1_out), .ld(Read__1____Write__0__Pin),
    .clr(Clear_Memory_out));  // open: din, sel
  Button Clear_Memory (.out(Clear_Memory_out));
  Hex_Digit_Display hex_digit_display_1 (.value(multiplexer_2_out));  // open: dp
  Multiplexer #(.width(4)) multiplexer_2 (
    .in0(4'b0001), .in1(4'b1010), .out(multiplexer_2_out), .sel(ram_1_data[0]), .en(1'b1));
  assign bit_extender_1_out = {{8{ram_1_data[15]}}, ram_1_data[15:8]};  // Bit_Extender bit_extender_1
  Bit_Extender #(.out_width(7)) bit_extender_2 (.in(ram_1_data[15:8]), .out(bit_extender_2_out));
  TTY tty_1 (.data(bit_extender_2_out), .clk(clock_1_out), .we(ram_1_data[2]), .clr(Clear_TTY_out));
  Button Clear_TTY (.out(Clear_TTY_out));

  // Notes on the sheet:
  //   Adder
endmodule
