// Logisim project CPE142_HW07_TheRegisterFile[PART02].circ as structural Verilog: 1 circuit, main circuit main
module main (
  input  Read__1
);

  wire button_1_out, button_2_out, clock_1_out, decoder_1_out0, decoder_1_out1, decoder_1_out2,
       decoder_1_out3, decoder_1_out4, not_1_out, or_1_out;
  wire [7:0] Accumulator_q, adder_2_out, multiplexer_2_out, ram_2_data;
  wire [15:0] adder_1_out, bit_extender_1_out, multiplexer_1_out, Program_Register_q, ram_1_data;

  Clock clock_1 (.out(clock_1_out));
  Register #(.width(16)) Program_Register (
    .D(adder_1_out), .en(1'b1), .Q(Program_Register_q), .clk(clock_1_out), .clr(button_2_out));
  assign bit_extender_1_out = {{8{ram_1_data[15]}}, ram_1_data[15:8]};  // Bit_Extender bit_extender_1
  not not_1 (not_1_out, Read__1);
  Multiplexer #(.width(16)) multiplexer_1 (
    .in0(16'h1), .in1(bit_extender_1_out), .out(multiplexer_1_out), .sel(decoder_1_out1));  // open: en
  Adder #(.width(16)) adder_1 (.a(Program_Register_q), .b(multiplexer_1_out), .out(adder_1_out));  // open: cin, cout
  RAM #(.addrWidth(16), .dataWidth(16), .bus("separate")) ram_1 (
    .addr(Program_Register_q), .data(ram_1_data), .str(not_1_out), .clk(clock_1_out), .ld(Read__1),
    .clr(button_1_out));  // open: din, sel
  Button button_1 (.out(button_1_out));
  TTY tty_1 (.data(ram_1_data[14:8]), .clk(clock_1_out), .we(decoder_1_out0), .clr(button_2_out));
  Decoder #(.select(3), .enable("false")) decoder_1 (
    .out0(decoder_1_out0), .out1(decoder_1_out1), .out2(decoder_1_out2), .out3(decoder_1_out3),
    .out4(decoder_1_out4), .sel(ram_1_data[2:0]));  // open: out5, out6, out7
  or or_1 (or_1_out, decoder_1_out2, decoder_1_out3);
  Register Accumulator (.D(adder_2_out), .en(or_1_out), .Q(Accumulator_q), .clk(clock_1_out), .clr(button_2_out));
  Multiplexer #(.width(8)) multiplexer_2 (
    .in0(Accumulator_q), .in1(ram_1_data[15:8]), .out(multiplexer_2_out), .sel(decoder_1_out3));  // open: en
  RAM #(.addrWidth(3), .bus("separate")) ram_2 (
    .addr(ram_1_data[7:5]), .din(Accumulator_q), .data(ram_2_data), .str(decoder_1_out4), .clk(clock_1_out),
    .clr(button_2_out));  // open: sel, ld
  Button button_2 (.out(button_2_out));
  Adder adder_2 (.a(multiplexer_2_out), .b(ram_2_data), .out(adder_2_out));  // open: cin, cout

  // Notes on the sheet:
  //   Adder
  //   Instruction RAM
  //   Write (0)
  //   Register File
  //   ALU
endmodule
