// Logisim project CPE142_HW09_TheConditionalBranch.circ as structural Verilog: 2 circuits, main circuit ALU
// 0
module main (
  input  Read__1
);

  wire and_1_out, button_2_out, clock, comparator_1_eq, Condition, D2, decoder_1_out0, decoder_1_out1,
       decoder_1_out3, decoder_1_out4, decoder_1_out5, not_1_out, or_1_out, reset;
  wire [6:0] TTY;
  wire [7:0] Accumulator_q, adder_2_out, alu_1_output, ram_1_data, ram_1_data_2, ram_2_data, undriven;
  wire [15:0] adder_1_out, bit_extender_1_out, multiplexer_1_out, Program_Register_q;

  Clock clock_1 (.out(clock));
  Button button_1 (.out(reset));
  Register #(.width(16)) Program_Register (
    .D(adder_1_out), .en(1'b1), .Q(Program_Register_q), .clk(clock), .clr(reset));
  not not_1 (not_1_out, Read__1);
  Multiplexer #(.width(16)) multiplexer_1 (
    .in0(16'h1), .in1(bit_extender_1_out), .out(multiplexer_1_out), .sel(and_1_out));  // open: en
  assign bit_extender_1_out = {{8{ram_1_data_2[7]}}, ram_1_data_2};  // Bit_Extender bit_extender_1
  and and_1 (and_1_out, decoder_1_out1, Condition);
  Adder #(.width(16)) adder_1 (.a(Program_Register_q), .b(multiplexer_1_out), .out(adder_1_out));  // open: cin, cout
  Decoder #(.select(3), .enable("false")) decoder_1 (
    .out0(decoder_1_out0), .out1(decoder_1_out1), .out2(D2), .out3(decoder_1_out3), .out4(decoder_1_out4),
    .out5(decoder_1_out5), .sel(ram_1_data[2:0]));  // open: out6, out7
  RAM #(.addrWidth(16), .dataWidth(16), .bus("separate")) ram_1 (
    .addr(Program_Register_q), .data({ram_1_data_2, ram_1_data}), .str(not_1_out), .clk(clock), .ld(Read__1),
    .clr(button_2_out));  // open: din, sel
  Button button_2 (.out(button_2_out));
  TTY tty_1 (.data(TTY), .clk(clock), .we(decoder_1_out0), .clr(reset));
  or or_1 (or_1_out, D2, decoder_1_out3, decoder_1_out4);
  Register Accumulator (.D(alu_1_output), .en(or_1_out), .Q(Accumulator_q), .clk(clock));  // open: clr
  RAM #(.addrWidth(3), .bus("separate")) ram_2 (
    .addr(ram_1_data[7:5]), .din(Accumulator_q), .data(ram_2_data), .str(decoder_1_out5), .clk(clock),
    .clr(reset));  // open: sel, ld
  ALU alu_1 (
    .Accumulator_Input(Accumulator_q), .Immediate_Input(ram_1_data_2), .Data_Reg_File_Input(ram_2_data),
    .Mux1_Input(decoder_1_out4), .Select_Input({D2, ram_1_data_2[7]}), .Output(alu_1_output));
  Comparator comparator_1 (.a(Accumulator_q), .b(ram_2_data), .eq(comparator_1_eq));  // open: gt, lt
  Multiplexer #(.width(7)) multiplexer_2 (
    .in0(Accumulator_q[6:0]), .in1(ram_1_data_2[6:0]), .out(TTY), .sel(ram_1_data_2[7]));  // open: en
  not not_2 (Condition, comparator_1_eq);
  Adder adder_2 (.b(undriven), .out(adder_2_out));  // open: a, cin, cout

  // Notes on the sheet:
  //   Write (0)
  //   Instruction RAM
  //   Adder
  //   Register File
  //   DECODER:
  //   0: Write TTY
  //   1: Offset Jump
  //   2: Accumulator / D Reg out
  //   3: Accumulator Enable
  //   4: Accumulator + Immediate
  //   5: Write Reg File
  //   INSTRUCTION OPCODE:
  //   0-2: Decoder
  //   5-7: Register Address
  //   8-15: Immediate
endmodule

module ALU (
  input  [7:0] Accumulator_Input,
  input  [7:0] Immediate_Input,
  input  [7:0] Data_Reg_File_Input,
  input  Mux1_Input,
  input  [1:0] Select_Input,
  output [7:0] Output
);

  wire [7:0] adder_1_out, bit_extender_1_out, divider_1_out, divider_1_rem, multiplexer_1_out;

  assign bit_extender_1_out = {{1{1'b0}}, Immediate_Input[6:0]};  // Bit_Extender bit_extender_1
  Multiplexer #(.width(8)) multiplexer_1 (
    .in0(Accumulator_Input), .in1(Immediate_Input), .out(multiplexer_1_out), .sel(Mux1_Input));  // open: en
  Adder adder_1 (.a(multiplexer_1_out), .b(Data_Reg_File_Input), .out(adder_1_out));  // open: cin, cout
  Divider divider_1 (
    .a(Accumulator_Input), .b(bit_extender_1_out), .out(divider_1_out), .rem(divider_1_rem));  // open: upper
  Multiplexer #(.select(2), .width(8)) multiplexer_2 (
    .in0(adder_1_out), .in1(adder_1_out), .in2(divider_1_out), .in3(divider_1_rem), .out(Output),
    .sel(Select_Input));  // open: en
endmodule
