// Logisim project CPE142_HW01_TheDataMemory.circ as structural Verilog: 1 circuit, main circuit main
module main (
);

  wire clock_1_out;
  wire [3:0] register_1_q, register_1_q_2;
  wire [7:0] adder_1_out;

  Clock clock_1 (.out(clock_1_out));
  Register register_1 (.D(adder_1_out), .en(1'b1), .Q({register_1_q_2, register_1_q}), .clk(clock_1_out), .clr(1'b0));
  Hex_Digit_Display hex_digit_display_1 (.value(register_1_q_2));  // open: dp
  Adder adder_1 (.a({register_1_q_2, register_1_q}), .b(8'h1), .out(adder_1_out));  // open: cin, cout
  Hex_Digit_Display hex_digit_display_2 (.value(register_1_q));  // open: dp
endmodule
