// Logisim project CPE142_HW03_TheSimpleStoredInstructionDecode.circ as structural Verilog: 1 circuit, main circuit main
module main (
  input  Write___Read_Pin
);

  wire Clear_Counter_out, Clear_Memory_out, clock_1_out, not_1_out;
  wire [3:0] multiplexer_1_out;
  wire [7:0] ram_1_data, random_1_out;
  wire [15:0] Counter_q;

  Counter #(.width(16), .max('hffff)) Counter (
    .count(1'b1), .Q(Counter_q), .clk(clock_1_out), .clr(Clear_Counter_out));  // open: load, D, carry
  Clock clock_1 (.out(clock_1_out));
  Button Clear_Counter (.out(Clear_Counter_out));
  Random random_1 (.clk(clock_1_out), .next(1'b1), .out(random_1_out), .clr(1'b0));
  not not_1 (not_1_out, Write___Read_Pin);
  RAM #(.addrWidth(16), .bus("separate")) ram_1 (
    .addr(Counter_q), .din(random_1_out), .data(ram_1_data), .str(not_1_out), .sel(1'b1), .clk(clock_1_out),
    .ld(Write___Read_Pin), .clr(Clear_Memory_out));
  Button Clear_Memory (.out(Clear_Memory_out));
  Multiplexer #(.width(4)) multiplexer_1 (
    .in0(4'b0001), .in1(4'b1010), .out(multiplexer_1_out), .sel(ram_1_data[0]), .en(1'b1));
  Hex_Digit_Display hex_digit_display_1 (.value(multiplexer_1_out));  // open: dp
endmodule
