// Logisim project CPE142_HW04_TheSimpleJump.circ as structural Verilog: 1 circuit, main circuit main
module main (
  input  Read__1____Write__0__Pin
);

  wire Clear_Counter_out, Clear_Memory_out, clock_1_out, clock_2_out, not_1_out;
  wire [3:0] multiplexer_2_out;
  wire [7:0] ram_1_data;
  wire [15:0] adder_1_out, multiplexer_1_out, Register_q;

  Register #(.width(16)) Register (
    .D(multiplexer_1_out), .en(1'b1), .Q(Register_q), .clk(clock_1_out), .clr(Clear_Counter_out));
  Clock clock_1 (.out(clock_1_out));
  Button Clear_Counter (.out(Clear_Counter_out));
  Adder #(.width(16)) adder_1 (.a(Register_q), .b(16'h1), .out(adder_1_out));  // open: cin, cout
  Multiplexer #(.width(16)) multiplexer_1 (
    .in0(adder_1_out), .in1(16'h1), .out(multiplexer_1_out), .sel(ram_1_data[1]));  // open: en
  not not_1 (not_1_out, Read__1____Write__0__Pin);
  Clock clock_2 (.out(clock_2_out));
  RAM #(.addrWidth(16), .bus("separate")) ram_1 (
    .addr(Register_q), .data(ram_1_data), .str(not_1_out), .clk(clock_2_out), .ld(Read__1____Write__0__Pin),
    .clr(Clear_Memory_out));  // open: din, sel
  Button Clear_Memory (.out(Clear_Memory_out));
  Hex_Digit_Display hex_digit_display_1 (.value(multiplexer_2_out));  // open: dp
  Multiplexer #(.width(4)) multiplexer_2 (
    .in0(4'b0001), .in1(4'b1010), .out(multiplexer_2_out), .sel(ram_1_data[0]), .en(1'b1));

  // Notes on the sheet:
  //   Adder
endmodule
