// Logisim project CPE142_HW06_TheRegisterFile[Part01].circ as structural Verilog: 1 circuit, main circuit main
module main (
  input  Read__1____Write__0__Pin
);

  wire Clear_2_out, Clear_3_out, Clear_4_out, Clear_out, clock_1_out, decoder_1_out1, decoder_1_out2,
       decoder_1_out3, not_1_out;
  wire [3:0] multiplexer_2_out;
  wire [7:0] adder_3_out, ram_1_data, ram_1_data_2, ram_2_data;
  wire [15:0] adder_1_out, adder_2_out, bit_extender_1_out, multiplexer_1_out, Program_Register_q;

  Clock clock_1 (.out(clock_1_out));
  Register #(.width(16)) Program_Register (
    .D(multiplexer_1_out), .en(1'b1), .Q(Program_Register_q), .clk(clock_1_out), .clr(Clear_out));
  Button Clear (.out(Clear_out));
  Adder #(.width(16)) adder_1 (.a(Program_Register_q), .b(16'h1), .out(adder_1_out));  // open: cin, cout
  Adder #(.width(16)) adder_2 (.a(Program_Register_q), .b(bit_extender_1_out), .out(adder_2_out));  // open: cin, cout
  assign bit_extender_1_out = {{8{ram_1_data_2[7]}}, ram_1_data_2};  // Bit_Extender bit_extender_1
  not not_1 (not_1_out, Read__1____Write__0__Pin);
  Multiplexer #(.width(16)) multiplexer_1 (
    .in0(adder_1_out), .in1(adder_2_out), .out(multiplexer_1_out), .sel(decoder_1_out2));  // open: en
  Decoder #(.select(3), .enable("false")) decoder_1 (
    .out1(decoder_1_out1), .out2(decoder_1_out2), .out3(decoder_1_out3), .sel(ram_1_data[2:0]));  // open: out0, out4, out5, out6, out7
  RAM #(.addrWidth(16), .dataWidth(16), .bus("separate")) ram_1 (
    .addr(Program_Register_q), .data({ram_1_data_2, ram_1_data}), .str(not_1_out), .clk(clock_1_out),
    .ld(Read__1____Write__0__Pin), .clr(Clear_2_out));  // open: din, sel
  Button Clear_2 (.out(Clear_2_out));
  TTY tty_1 (.data(ram_1_data_2[6:0]), .clk(clock_1_out), .we(decoder_1_out1), .clr(Clear_3_out));
  Button Clear_3 (.out(Clear_3_out));
  RAM #(.addrWidth(3), .bus("separate")) ram_2 (
    .addr(ram_1_data[7:5]), .din(adder_3_out), .data(ram_2_data), .str(decoder_1_out3), .clk(clock_1_out),
    .clr(Clear_4_out));  // open: sel, ld
  Button Clear_4 (.out(Clear_4_out));
  Adder adder_3 (.a(ram_1_data_2), .b(ram_2_data), .out(adder_3_out));  // open: cin, cout
  Multiplexer #(.width(4)) multiplexer_2 (
    .in0(4'b0001), .in1(4'b1010), .out(multiplexer_2_out), .en(1'b1));  // open: sel
  Hex_Digit_Display hex_digit_display_1 (.value(multiplexer_2_out));  // open: dp

  // Notes on the sheet:
  //   Adder
  //   Instruction RAM
  //   Register File
endmodule
