// Logisim project stallable_mem.circ as structural Verilog: 1 circuit, main circuit StallableMemory
module StallableMemory (
  input  [7:0] Address,
  input  [7:0] data_in,
  input  store,
  input  load,
  input  clear,
  input  clock,
  output [7:0] data_out,
  output Ready
);

  wire and_1_out, not_1_out, or_1_out;
  wire [7:0] adder_1_out, multiplexer_1_out, state_counter_q;

  or or_1 (or_1_out, store, load);
  and and_1 (and_1_out, not_1_out, or_1_out);
  Multiplexer #(.width(8), .enable("false")) multiplexer_1 (
    .in0({8{1'b0}}), .in1(adder_1_out), .out(multiplexer_1_out), .sel(and_1_out));
  RAM #(.bus("separate")) ram_1 (
    .addr(Address), .din(data_in), .data(data_out), .str(store), .sel(1'b1), .clk(clock), .ld(1'b1),
    .clr(clear));
  Register state_counter (.D(multiplexer_1_out), .en(1'b1), .Q(state_counter_q), .clk(clock), .clr(clear));
  not not_1 (not_1_out, Ready);
  Adder adder_1 (.a(state_counter_q), .b(8'h1), .out(adder_1_out));  // open: cin, cout
  Comparator #(.mode("unsigned")) comparator_1 (.a(state_counter_q), .b(8'h6), .eq(Ready));  // open: gt, lt
  Hex_Digit_Display hex_digit_display_1 (.value(state_counter_q[7:4]));  // open: dp
  Hex_Digit_Display hex_digit_display_2 (.value(state_counter_q[3:0]));  // open: dp
  LED led_1 (.in(Ready));

  // Notes on the sheet:
  //   delay counter
  //   stall time per request
endmodule
